# Fritzing sketch DSU Button (saved by Fritzing 0.9.3b)
perfboards: 1

parts:
  Part1 = Arduino Uno (Rev3)
  U1 = 2-Channel 5v Relay Shield [package=relay-2ch5v10a]
  J2 = male pin header, 7 pins [form="♂ (male)"]

nets:
  N1: Part1.D9_PWM, J2.pin3
  N2: Part1.D11_PWM/MOSI, J2.pin5
  N3: Part1.D12/MISO, J2.pin4
  N4: Part1.D13/SCK, J2.pin6
  GND: Part1.GND, U1.GND, J2.pin2
  N5: Part1.D5_PWM, U1.IN1
  N6: Part1.D6_PWM, U1.IN2
  N7: Part1.3V3, J2.pin1
  5V: Part1.5V, U1.VCC

notes:
  Cable
  DSU

custom parts:
  2-Channel 5v Relay Shield: 2 Channel 5v Relay Shield w. 2x SPD-06VDC-SD-C
